# Fritzing sketch frtizing (saved by Fritzing 0.9.3b)
breadboards: 1

parts:
  Componente1 = Arduino Uno (Rev3)
  S1 = Momentary Switch [package=ksa_sealed_tac_switch]
  LED6 = LED - 5mm [color="Red (633nm)" package="5 mm [THT]"]

nets:
  N1: Componente1.D10_PWM/SS, LED6.anode
  N2: Componente1.D11_PWM/MOSI, LED6.cathode
  N3: Componente1.D7, S1.2
  N4: Componente1.5V, S1.4
